// Logisim project assign1bonus (1).circ as structural Verilog: 2 circuits, main circuit main
module main (
  input  in_1,
  input  in_2,
  input  in_3,
  input  in_4,
  output a,
  output b,
  output c,
  output d,
  output e,
  output f,
  output g
);

  wire A_prime_B_out, A_prime_B_prime_D_prime_out, A_prime_B_prime_out, A_prime_BC_prime_out, A_prime_BD_out,
       A_prime_C_out, A_prime_C_prime_D_prime_out, A_prime_C_prime_out, A_prime_CD_out, A_prime_D_out,
       AB_out, AB_prime_C_prime_out, AB_prime_out, AC_out, AC_prime_D_out, AC_prime_out, AD_out,
       AD_prime_out, B_prime_C_out, B_prime_CD_out, B_prime_D_prime_out, BC_out, BC_prime_D_out,
       BCD_prime_out, BD_prime_out, C_prime_D_2_out, C_prime_D_out, CD_prime_out, not_1_out, not_2_out,
       not_3_out, not_4_out;

  not not_1 (not_1_out, in_1);
  not not_2 (not_2_out, in_2);
  not not_3 (not_3_out, in_3);
  and A_prime_B_prime (A_prime_B_prime_out, not_1_out, not_2_out);
  and A_prime_B (A_prime_B_out, not_1_out, in_2);
  and AB_prime (AB_prime_out, in_1, not_2_out);
  and AB (AB_out, in_1, in_2);
  not not_4 (not_4_out, in_4);
  and BC (BC_out, in_2, in_3);
  and AB_prime_C_prime (AB_prime_C_prime_out, in_1, not_3_out, not_2_out);
  and A_prime_C_prime (A_prime_C_prime_out, not_1_out, not_3_out);
  and AC_prime (AC_prime_out, not_3_out, in_1);
  and AC (AC_out, in_1, in_3);
  and A_prime_BC_prime (A_prime_BC_prime_out, in_2, not_1_out, not_3_out);
  and B_prime_C (B_prime_C_out, not_2_out, in_3);
  and B_prime_D_prime (B_prime_D_prime_out, not_2_out, not_4_out);
  and A_prime_C (A_prime_C_out, not_1_out, in_3);
  and A_prime_BD (A_prime_BD_out, not_1_out, in_2, in_4);
  and A_prime_C_prime_D_prime (A_prime_C_prime_D_prime_out, not_3_out, not_1_out, not_4_out);
  and A_prime_CD (A_prime_CD_out, not_1_out, in_3, in_4);
  and A_prime_D (A_prime_D_out, not_1_out, in_4);
  and A_prime_B_prime_D_prime (A_prime_B_prime_D_prime_out, not_4_out, not_2_out, not_1_out);
  and CD_prime (CD_prime_out, in_3, not_4_out);
  and BD_prime (BD_prime_out, in_2, in_2, not_4_out);
  and AD (AD_out, in_4, in_1);
  and AD_prime (AD_prime_out, not_4_out, in_1);
  and AC_prime_D (AC_prime_D_out, in_4, in_1, not_3_out);
  and C_prime_D (C_prime_D_out, in_4, not_3_out);
  and B_prime_CD (B_prime_CD_out, in_4, in_3, not_2_out);
  and C_prime_D_2 (C_prime_D_2_out, not_4_out, not_3_out);
  and BC_prime_D (BC_prime_D_out, in_4, in_2, not_3_out);
  and BCD_prime (BCD_prime_out, not_4_out, in_3, in_2);
  or u_c (c, C_prime_D_out, AB_prime_out, A_prime_C_prime_out, A_prime_D_out, A_prime_B_out);
  or or_1 (e, AB_out, B_prime_D_prime_out, CD_prime_out, AC_out);
  or u_f (f, C_prime_D_2_out, BD_prime_out, AB_prime_out, AC_out, A_prime_BC_prime_out);
  or u_g (g, B_prime_C_out, CD_prime_out, AB_prime_out, AD_out, A_prime_BC_prime_out);
  or u_a (a, AB_prime_C_prime_out, B_prime_D_prime_out, A_prime_C_out, BC_out, AD_prime_out, A_prime_BD_out);
  or u_b (b, B_prime_D_prime_out, AC_prime_D_out, A_prime_CD_out, A_prime_C_prime_D_prime_out, A_prime_B_prime_out);
  or u_d (d, AC_prime_out, A_prime_B_prime_D_prime_out, A_prime_B_prime_D_prime_out, B_prime_CD_out, BCD_prime_out, BC_prime_D_out);
endmodule

module assign1bonus (
);

  wire button_1_out, main_1_a, main_1_b, main_1_c, main_1_d, main_1_e, main_1_f, main_1_g;
  wire [3:0] counter_1_q;

  Button button_1 (.out(button_1_out));
  Counter #(.width(4), .max('hf)) counter_1 (.Q(counter_1_q), .clk(button_1_out));  // open: load, D, count, carry, clr
  main main_1 (
    .in_1(counter_1_q[3]), .in_2(counter_1_q[2]), .in_3(counter_1_q[1]), .in_4(counter_1_q[0]), .a(main_1_a),
    .b(main_1_b), .c(main_1_c), .d(main_1_d), .e(main_1_e), .f(main_1_f), .g(main_1_g));
  _7_Segment_Display u_7_segment_display_1 (
    .g(main_1_g), .f(main_1_f), .a(main_1_a), .b(main_1_b), .e(main_1_e), .d(main_1_d), .c(main_1_c));  // open: dp
endmodule
